# Fritzing sketch SRCS_schematic (saved by Fritzing 1.0.1rc)

parts:
  J1 = STM32 Nucleo boards
  TXS0108E_8-Bit_Bi-directional_Level-Shifting_Voltage_Translator1 = TXS0108 [part_number=TXS0108EPW package=TSSOP]
  DHT1 = DHT11 Humitidy and Temperature Sensor (3 pins)
  Driver1 = 28BYJ-48 Driver Module [part_number=ULN2003 package=THT]
  SM1 = 28BYJ-48 Stepper Motor [part_number=28BYJ-48]
  M1 = DC Motor [voltage_(max)=6V voltage_(min)=3V]
  Part1 = Arduino Ethernet Shield (Rev3)
  U1 = LM2596 step down module
  U2 = LM2596 step down module
  R2 = Photocell (LDR) [package=THT]
  R3 = Resistor [tolerance=±5% power=0.25 resistance=4.7K package=THT]
  D1 = Rectifier Diode [part_number=1N4001 package="300 mil [THT]"]

nets:
  N1: J1.PC7, R2.pin_1, R3.Pin_0
  N2: J1.PA9, TXS0108E_8-Bit_Bi-directional_Level-Shifting_Voltage_Translator1.A1
  N3: J1.PA8, TXS0108E_8-Bit_Bi-directional_Level-Shifting_Voltage_Translator1.A2
  N4: J1.PB10, TXS0108E_8-Bit_Bi-directional_Level-Shifting_Voltage_Translator1.A3
  N5: J1.PB4, TXS0108E_8-Bit_Bi-directional_Level-Shifting_Voltage_Translator1.A4
  N6: J1.PB3, DHT1.Signal
  N7: J1.PA10, M1.pin_2
  N8: J1.VIN, U1.OUT+
  N9: TXS0108E_8-Bit_Bi-directional_Level-Shifting_Voltage_Translator1.VccA, TXS0108E_8-Bit_Bi-directional_Level-Shifting_Voltage_Translator1.OE, R2.pin_0
  GND: TXS0108E_8-Bit_Bi-directional_Level-Shifting_Voltage_Translator1.GND, DHT1.Gnd, Driver1.GND, Part1.GND, U1.IN-, U1.OUT-, U2.IN-, U2.OUT-, R3.Pin_1, D1.anode
  N10: TXS0108E_8-Bit_Bi-directional_Level-Shifting_Voltage_Translator1.B4, Driver1.IN4
  N11: TXS0108E_8-Bit_Bi-directional_Level-Shifting_Voltage_Translator1.B3, Driver1.IN3
  N12: TXS0108E_8-Bit_Bi-directional_Level-Shifting_Voltage_Translator1.B2, Driver1.IN2
  N13: TXS0108E_8-Bit_Bi-directional_Level-Shifting_Voltage_Translator1.VccB, DHT1.Plus, Part1.5V
  N14: TXS0108E_8-Bit_Bi-directional_Level-Shifting_Voltage_Translator1.B1, Driver1.IN1
  N15: Driver1.Vmotor, U2.OUT+
  N16: Driver1.blue-pin, SM1.blue-pin
  N17: Driver1.pink-pin, SM1.pink-pin
  N18: Driver1.yellow-pin, SM1.yellow-pin
  N19: Driver1.orange-pin, SM1.orange-pin
  N20: Driver1.red-pin, SM1.red-pin
  N21: Part1.ICSP_MISO, Part1.SPI/D12
  N22: Part1.ICSP_SCK, Part1.SPI/D13
  N23: Part1.ICSP_MOSI, Part1.PWM_D11

notes:
  Anemometer
  7v < V < 9v
  DHT11
  5v
  LightSensor
  TXS108E
  ULN2003
  28BYJ-48
  (Mount)

custom parts:
  TXS0108: This 8-bit non-inverting translator uses two separate configurable power-supply rails. The A port tracks the VCCA pin supply voltage. The VCCA pin accepts any supply voltage between 1.2 V and 3.6 V. The B port tracks the VCCB pin supply voltage. The VCCB pin accepts any supply voltage between 1.65 V and 5.5 V. Two input supply pins allows for low Voltage bidirectional translation between any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
  DHT11 Humitidy and Temperature Sensor (3 pins): DHT11 Humidity and Temperature Sensor (3 pins).
  28BYJ-48 Driver Module: High-power ULN2003 Stepper Motor Driver Board Test Module For Arduino AVR SMD
  28BYJ-48 Stepper Motor: Unipolar Stepper Motor 28BYJ-48 Top coil - pink & orange Bottom coil - blue & yellow Common rail - red Connector pins: blue - pink - yellow - orange - red
  LM2596 step down module: LM2596 DC-DC step down power supply module 3 A.
